# Fritzing sketch Untitled Sketch 2 (saved by Fritzing 0.9.3b)
breadboards: 1

parts:
  R3 = Resistor [tolerance=±5% resistance=1k package=THT]
  R2 = Resistor [tolerance=±5% resistance=33k package=THT]
  C1 = Electrolytic Capacitor [capacitance=22µF package="100 mil [THT, electrolytic]"]
  U1 = 555 Timer [package="DIP8 [THT]"]
  LED1 = LED - 5mm [color="Red (633nm)" package="5 mm [THT]"]
  R1 = Resistor [tolerance=±5% resistance=470 package=THT]
  S1 = Pushbutton [package="[THT]"]  # not connected

nets (from the breadboard view):
  N1: R3.Pin_0, U1.Pin_4, U1.Pin_8
  N2: R3.Pin_1, R2.Pin_0, U1.Pin_7
  N3: R2.Pin_1, C1.-, U1.Pin_2, U1.Pin_6
  N4: C1.+, U1.Pin_1, LED1.cathode
  N5: U1.Pin_3, R1.Pin_1
  N6: LED1.anode, R1.Pin_0
